# Fritzing sketch pcbrap (saved by Fritzing 0.9.3b)
breadboards: 1

parts:
  Mod1 = Raspberry Pi Pico
  IC1 = L293D [package=THT]
  M1 = DC Motor
  D1 = Schottky Diode [part_number=1N5817 package="300 mil [THT]"]
  YwRobot_Power_Supply1 = YwRobot Breadboard Power Supply [part_number=545043]

nets:
  N1: Mod1.pin_1, IC1.In_1
  N2: Mod1.pin_2, IC1.In_2
  N3: Mod1.pin_3, Mod1.pin_8, Mod1.pin_13, Mod1.pin_18, Mod1.pin_23, Mod1.pin_28, Mod1.pin_33, Mod1.pin_38, IC1.0V, YwRobot_Power_Supply1.VCC
  N4: Mod1.pin_39, D1.cathode
  N5: IC1.Enable_1, IC1.+Vmotor, IC1.Enable_2, IC1.+V, YwRobot_Power_Supply1.GND#13, YwRobot_Power_Supply1.GND#14
  N6: IC1.Out_1_(_Controlled_by_Enable_1_), M1.pin_2
  N7: IC1.Out_2_(_Controlled_by_Enable_1_), M1.pin_1
  N8: D1.anode, YwRobot_Power_Supply1.GND#11, YwRobot_Power_Supply1.GND#12

custom parts:
  Raspberry Pi Pico: Raspberry Pi Pico. Based around the RP2040 microcontroller the Pico is a low cost microcontroller device bringing Raspberry Pi quality, cost, and easy of use to the microcontroller space. Jan 2021, Split part in to two versions: SMD (this one) and tht. This one is single sided and uses the castellation pads to solder the module to the board (no holes, other than for the USB connector!). The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
  YwRobot Breadboard Power Supply: The YwRobot Breadboard Power Supply (MB-V2) has two power rails; they can be 5V or 3V3. Power to the module can be provided through the female USB socket or through the A10 (female) 2.1mm power jack.
